// Logisim project sc1v2.circ as structural Verilog: 1 circuit, main circuit main
module main (
  input  x1,
  input  x2,
  input  x3,
  output d,
  output b
);

  wire not_1_out, not_2_out, not_3_out, not_4_out, not_5_out, or_1_out, or_2_out, or_3_out, or_4_out,
       or_5_out, or_6_out, or_7_out;

  not not_1 (not_1_out, x2);
  not not_2 (not_2_out, x3);
  not not_3 (not_3_out, x1);
  not not_4 (not_4_out, x3);
  not not_5 (not_5_out, x1);
  or or_1 (or_1_out, x1, x2);
  or or_2 (or_2_out, x1, x3);
  or or_3 (or_3_out, x2, x3);
  or or_4 (or_4_out, x1, x2, x3);
  or or_5 (or_5_out, x1, not_1_out, not_2_out);
  or or_6 (or_6_out, not_3_out, x2, not_4_out);
  or or_7 (or_7_out, not_5_out, x2, x3);
  and and_1 (b, or_1_out, or_2_out, or_3_out);
  and and_2 (d, or_4_out, or_5_out, or_6_out, or_7_out);
endmodule
