// Logisim project sc2.circ as structural Verilog: 1 circuit, main circuit main
module main (
  input  x1,
  input  x2,
  input  x3,
  input  x4,
  output O4,
  output O3,
  output O2,
  output O1
);

  wire not_1_out, not_2_out, not_3_out, not_4_out, not_5_out, not_6_out, not_7_out, not_8_out, not_9_out,
       not_10_out, not_11_out, not_12_out, not_13_out, or_1_out, or_2_out, or_3_out, or_4_out, or_5_out,
       or_6_out, or_7_out, or_8_out;

  not not_1 (not_1_out, x2);
  not not_2 (not_2_out, x1);
  not not_3 (not_3_out, x3);
  not not_4 (not_4_out, x2);
  not not_5 (not_5_out, x3);
  not not_6 (not_6_out, x1);
  not not_7 (not_7_out, x1);
  not not_8 (not_8_out, x2);
  not not_9 (not_9_out, x3);
  not not_10 (not_10_out, x1);
  not not_11 (not_11_out, x3);
  not not_12 (not_12_out, x1);
  not not_13 (not_13_out, x2);
  or or_1 (or_1_out, x1, x2);
  or or_2 (or_2_out, not_1_out, x3);
  or or_3 (or_3_out, not_2_out, not_3_out);
  or or_4 (or_4_out, x2, x3);
  or or_5 (or_5_out, not_4_out, not_5_out);
  or or_6 (or_6_out, not_7_out, not_8_out);
  or or_7 (or_7_out, not_10_out, not_11_out);
  or or_8 (or_8_out, not_12_out, not_13_out);
  and and_1 (O4, or_1_out, or_2_out, or_3_out);
  and and_2 (O3, or_4_out, or_5_out, not_6_out);
  and and_3 (O2, or_6_out, not_9_out);
  and and_4 (O1, or_7_out, or_8_out, x4);
endmodule
