// Logisim project Sc1.circ as structural Verilog: 2 circuits, main circuit main
module main (
  output out_1,
  output out_2,
  output out_3,
  output out_4,
  output out_5,
  output out_6
);

  wire and_1_out, and_2_out, button_1_out, button_2_out;

  Button button_1 (.out(button_1_out));
  and and_1 (and_1_out, button_1_out, out_3, out_5);
  and and_2 (and_2_out, button_1_out, out_5);
  Button button_2 (.out(button_2_out));
  T_flip_flop t_flip_flop_1 (.Out(out_1), .inv_Out(out_2), .Clock(and_1_out), .in_1(button_2_out));
  T_flip_flop t_flip_flop_2 (.Out(out_3), .inv_Out(out_4), .Clock(and_2_out), .in_1(button_2_out));
  T_flip_flop t_flip_flop_3 (.Out(out_5), .inv_Out(out_6), .Clock(button_1_out), .in_1(button_2_out));

  // Notes on the sheet:
  //   SET
  //   q1 = !V
  //   q2 = !q1 & !V
  //   q3 = !q2 & !q1 & !V
  //   которого построена в соответствии с системой выражений:
  //   Функиональная схема двоичного вычитающего счётчика на 8 внутренних состояний, 
endmodule

module T_flip_flop (
  input  in_1,
  input  Clock,
  output Out,
  output inv_Out
);

  wire nand_1_out, nand_2_out, nand_3_out, nand_4_out, nand_5_out, nand_6_out, not_1_out, not_2_out, or_1_out;

  not not_1 (not_1_out, in_1);
  or or_1 (or_1_out, in_1, Clock);
  nand nand_1 (nand_1_out, inv_Out, or_1_out);
  nand nand_2 (nand_2_out, nand_1_out, or_1_out);
  not not_2 (not_2_out, or_1_out);
  nand nand_3 (nand_3_out, nand_1_out, nand_4_out);
  nand nand_4 (nand_4_out, nand_3_out, nand_2_out);
  nand nand_5 (nand_5_out, nand_3_out, not_2_out);
  nand nand_6 (nand_6_out, not_2_out, nand_4_out);
  nand nand_7 (Out, nand_5_out, not_1_out, inv_Out);
  nand nand_8 (inv_Out, Out, nand_6_out);
endmodule
